# Fritzing sketch Helmet Circuit (saved by Fritzing 0.9.3b)

parts:
  HUD_OLED = Grove OLED 128x96
  ATtiny85 = ATTINY13 [package=dip]
  USB_Mic_1 = Breakout Board for Electret Microphone  # not connected
  Play/Pause = Pushbutton [package="[SMD]"]
  FS1000A = FS1000A - 433Mhz RF Transmitter [package=THT]
  Part13 = MQ-3 breakout
  SMD_Mosfet = MOSFET-PCHANNEL [package=sot23-3]
  SMD_R1 = Resistor [tolerance=±5% resistance=4.7k package="0805 [SMD]"]  # not connected
  R2 = Resistor [tolerance=±5% resistance=4.7k package="0805 [SMD]"]  # not connected
  R4 = Resistor [tolerance=±5% resistance=2.2 package="0603 [SMD]"]
  R3 = Resistor [tolerance=±5% resistance=2.2 package="0603 [SMD]"]
  Type_C_Port = Adafruit USB Type C Breakout [part_number=4090]
  IP5306 = IC, DIP package, 8 pins [chip_label=IP5306]
  SMD_Ind_L1 = Inductors [package=c0402]
  C3 = Capacitor [package=0805]  # not connected
  SMD_Cap_C7 = Capacitor [package=0805]
  C6 = Capacitor [package=0805]
  C5 = Capacitor [package=0805]
  C4 = Capacitor [package=0805]
  C2 = Capacitor [package=0805]  # not connected
  C1 = Capacitor [package=0805]
  68K = Resistor [tolerance=±5% resistance=68k package="0603 [SMD]"]  # not connected
  15K = Resistor [tolerance=±5% resistance=15k package="0603 [SMD]"]  # not connected
  C7 = Ceramic Capacitor [capacitance=100nF package="200 mil [THT, multilayer]"]  # not connected
  IC2 = IC, DIP package, 16 pins [chip_label=PAM8407]
  C8 = Capacitor [package=0805]
  C7_2 = Capacitor [package=0805]
  C6_2 = Capacitor [package=0805]
  C5_2 = Capacitor [package=0805]
  C4_2 = Capacitor [package=0805]
  C3_2 = Capacitor [package=0805]
  C2_2 = Capacitor [package=0805]
  SMD_Cap_C1 = Capacitor [package=0805]
  Volume_- = Pushbutton [package="[SMD]"]
  Volume_+ = Pushbutton [package="[SMD]"]
  Bone_Conduction_Transducer_Left = Vibration Motor- ROB-08449 [package=vibe-motor-10mm]
  Bone_Conduction_Transducer_Right = Vibration Motor- ROB-08449 [package=vibe-motor-10mm]
  TRM1 = Terminal 2pin  # not connected
  IC3 = MCP3008 8-channel 10-bit ADC [part_number=MCP3008]
  IC4 = IC, DIP package, 10 pins [chip_label=MCP4728]
  SMD_Cap_C1_2 = Capacitor [package=0805]
  C2_3 = Capacitor [package=0805]
  R1 = Resistor [tolerance=±5% resistance=10k package="0805 [SMD]"]
  R2_2 = Resistor [tolerance=±5% resistance=10k package="0805 [SMD]"]
  U16 = LIPO-2000mAh [package=lipo-2000]
  Raspberry_Pi_Zero1 = Raspberry Pi Zero
  GY1 = MPU-6050 Board GY-521 [form="♀ (female)" package=THT]  # not connected
  S1 = SWITCH-MOMENTARY-2 [package=tactile-pth-12mm]

nets:
  N1: HUD_OLED.SDA, Raspberry_Pi_Zero1.GPIO2
  N2: HUD_OLED.SCL, Raspberry_Pi_Zero1.GPIO3
  N3: ATtiny85.PB5(NRES), S1.1
  N4: ATtiny85.PB3(ADC3), Raspberry_Pi_Zero1.GPIO17
  N5: ATtiny85.GND, S1.2
  N6: ATtiny85.PB2(SCK_ADC1), SMD_Mosfet.G
  N7: ATtiny85.VCC, IP5306.pin8
  N8: Play/Pause.Pin_4, Raspberry_Pi_Zero1.GPIO4
  N9: FS1000A.DATA, Raspberry_Pi_Zero1.GPIO12
  N10: Part13.AO, IC3.no_name_yet#16
  N11: R4.Pin_1, C4.2
  N12: R3.Pin_1, C1.2
  N13: Type_C_Port.VBUS, Type_C_Port.SBU2, IP5306.pin1, IP5306.pin2
  N14: Type_C_Port.D-, Type_C_Port.D+, Type_C_Port.SBU1
  N15: IP5306.pin6, SMD_Ind_L1.1
  N16: IP5306.pin7, SMD_Ind_L1.2
  N17: SMD_Cap_C7.1, C6.1, C5.1, C4.1, U16.-
  N18: IC2.pin1, SMD_Cap_C1.1
  N19: IC2.pin2, C2_2.1
  N20: IC2.pin4, Volume_+.Pin_1, Volume_+.Pin_2
  N21: IC2.pin5, Volume_-.Pin_1, Volume_-.Pin_2
  N22: IC2.pin7, C3_2.1
  N23: IC2.pin8, C4_2.1
  N24: IC2.pin9, IC2.pin16, C8.2, C7_2.2
  N25: IC2.pin10, C6_2.2
  N26: IC2.pin11, Bone_Conduction_Transducer_Left.+
  N27: IC2.pin12, IC2.pin13
  N28: IC2.pin14, Bone_Conduction_Transducer_Right.+
  N29: IC2.pin15, C5_2.2
  N30: C6_2.1, Bone_Conduction_Transducer_Left.-
  N31: C5_2.1, Bone_Conduction_Transducer_Right.-
  N32: C4_2.2, IC4.pin7
  N33: SMD_Cap_C1.2, IC4.pin6
  N34: Volume_-.Pin_4, Volume_+.Pin_4
  N35: IC3.no_name_yet#2, Raspberry_Pi_Zero1.GPIO22
  N36: IC3.no_name_yet#3, Raspberry_Pi_Zero1.GPIO10
  N37: IC3.no_name_yet#4, Raspberry_Pi_Zero1.GPIO9
  N38: IC3.no_name_yet#5, Raspberry_Pi_Zero1.GPIO11
  N39: IC3.no_name_yet#7, IC3.no_name_yet#8
  N40: IC4.pin1, SMD_Cap_C1_2.2, C2_3.2
  N41: IC4.pin2, R1.Pin_1
  N42: IC4.pin3, IC4.pin4, R2_2.Pin_1
  N43: IC4.pin10, SMD_Cap_C1_2.1, C2_3.1
  N44: R1.Pin_0, R2_2.Pin_0

custom parts:
  FS1000A - 433Mhz RF Transmitter: This is 433Mhz RF transmitter with receiver kit for Arduino ARM MCU wireless Application environment: Remote control switch, receiver module, motorcycles, automobile anti-theft products, home security products, electric doors, shutter doors, windows, remote control socket, remote control LED, remote audio remote control electric doors, garage door remote control, remote control retractable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
  MQ-3 breakout: Alcohol sensor is capable of detecting alcohol (ethanol) particles on itself and gives the information in digital form back to us to manipulate with it. SKU:101251 • Voltage: 5V DC • Power: max 750mW • Measurement range: 0.04-4mg/L
  Adafruit USB Type C Breakout: Adafruit breakout board for USB Type C socket.
  Terminal 2pin: 2-pin Terminal Block
  MPU-6050 Board GY-521: Acelerometro y Giroscopio MPU-6050 Board GY-521
