# Fritzing sketch Vehicle Circuit (saved by Fritzing 0.9.3b)
breadboards: 1

parts:
  Part2 = u-blox NEO-6M GPS Breakout
  LM_2596_-_4_1V_O/P = LM2596 step down module
  SIM800L_BO1 = SIM800L BO
  R1 = Resistor [tolerance=±10% resistance=10k package=THT]
  R2 = Resistor [tolerance=±10% resistance=20k package=THT]
  Arduino_Pro_mini = Arduino Pro Mini v13
  7805_IC = Voltage Regulator [package=to220-igo]
  D1 = Zener Diode [part_number=1N4732A breakdown_voltage=3.6V package="300 mil [THT]"]
  C2 = Capacitor Polarized [package=cpol-radial-100uf-25v]
  C6 = Electrolytic Capacitor [capacitance=100μF package="0807 [SMD, electrolytic]"]
  C7 = Electrolytic Capacitor [capacitance=1000μF package="1010 [SMD, electrolytic]"]
  C8 = Electrolytic Capacitor [capacitance=1000μF package="1010 [SMD, electrolytic]"]
  FS_1000A_Receiver = XD-RF-5V [package=THT]
  D2 = Diode [package=diode-1n4001]  # not connected
  Q1 = TRANSISTOR_NPN [package=to-92-ammo]
  Q2 = TRANSISTOR_NPN [package=to-92-ammo]
  J1 = Piezo Speaker
  MOTOR1 = Vibration Motor

nets:
  GND: Part2.GND, LM_2596_-_4_1V_O/P.IN-, LM_2596_-_4_1V_O/P.OUT-, SIM800L_BO1.pin_6, R2.Pin_0, 7805_IC.IN, D1.anode, C2.+, C6.-, C7.-, C8.-, FS_1000A_Receiver.GND, Q1.E, Q2.E
  N1: Part2.VCC, Arduino_Pro_mini.RAW, 7805_IC.OUT, MOTOR1.POS
  N2: Part2.TXD, Arduino_Pro_mini.D1/RX
  N3: LM_2596_-_4_1V_O/P.IN+, D1.cathode, J1.pin2
  N4: LM_2596_-_4_1V_O/P.OUT+, SIM800L_BO1.PIN2, C6.+, C7.+, C8.+
  N5: SIM800L_BO1.pin_4, R1.Pin_1, R2.Pin_1
  N6: SIM800L_BO1.pin_5, Arduino_Pro_mini.D2
  N7: Arduino_Pro_mini.D9_PWM, Q2.B
  N8: Arduino_Pro_mini.D6_PWM, Q1.B
  N9: Arduino_Pro_mini.D4, FS_1000A_Receiver.DATA
  N10: 7805_IC.GND, C2.-
  N11: Q1.C, MOTOR1.NEG
  N12: Q2.C, J1.pin1

notes:
  Vehicle Battery
  + -

custom parts:
  LM2596 step down module: LM2596 DC-DC step down power supply module 3 A.
  XD-RF-5V: This is 433Mhz RF transmitter with receiver kit for Arduino ARM MCU wireless Application environment: Remote control switch, receiver module, motorcycles, automobile anti-theft products, home security products, electric doors, shutter doors, windows, remote control socket, remote control LED, remote audio remote control electric doors, garage door remote control, remote control retractable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
  Vibration Motor: An eccentric vibration motor!
