# Fritzing sketch IP5306 Charging Module (saved by Fritzing 0.9.3b)

parts:
  IP5306 = IC, DIP package, 8 pins [chip_label=IP5306]
  SMD_Ind_L1 = Inductors [package=c0402]
  C1 = Capacitor [package=0805]
  C2 = Capacitor [package=0805]  # not connected
  C4 = Capacitor [package=0805]
  C3 = Capacitor [package=0805]  # not connected
  Type_C_Port = Adafruit USB Type C Breakout [part_number=4090]
  R2 = Resistor [tolerance=±5% resistance=4.7k package="0805 [SMD]"]  # not connected
  R3 = Resistor [tolerance=±5% resistance=2.2 package="0603 [SMD]"]
  R4 = Resistor [tolerance=±5% resistance=2.2 package="0603 [SMD]"]
  C5 = Capacitor [package=0805]
  C6 = Capacitor [package=0805]
  SMD_Cap_C7 = Capacitor [package=0805]
  SMD_R1 = Resistor [tolerance=±5% resistance=4.7k package="0805 [SMD]"]  # not connected

nets:
  N1: IP5306.pin1, Type_C_Port.VBUS
  N2: IP5306.pin6, SMD_Ind_L1.1
  N3: IP5306.pin7, SMD_Ind_L1.2
  N4: C1.2, R3.Pin_1
  N5: C4.1, C5.1, C6.1, SMD_Cap_C7.1
  N6: C4.2, R4.Pin_1
  N7: Type_C_Port.D-, Type_C_Port.D+

custom parts:
  Adafruit USB Type C Breakout: Adafruit breakout board for USB Type C socket.
