# Fritzing sketch MCP4728 DAC (saved by Fritzing 0.9.3b)

parts:
  IC2 = IC, DIP package, 10 pins [chip_label=MCP4728]
  SMD_Cap_C1 = Capacitor [package=0805]
  R1 = Resistor [tolerance=±5% resistance=10k package="0805 [SMD]"]
  C2 = Capacitor [package=0805]
  R2 = Resistor [tolerance=±5% resistance=10k package="0805 [SMD]"]

nets:
  N1: IC2.pin1, SMD_Cap_C1.2, C2.2
  N2: IC2.pin2, R1.Pin_1
  N3: IC2.pin3, R2.Pin_1
  N4: IC2.pin10, SMD_Cap_C1.1, C2.1
  N5: R1.Pin_0, R2.Pin_0
