# Fritzing sketch PAM8407 Audio Amp (saved by Fritzing 0.9.3b)

parts:
  IC1 = IC, DIP package, 16 pins [chip_label=PAM8407]
  SMD_Cap_C1 = Capacitor [package=0805]
  C2 = Capacitor [package=0805]
  Volume_+ = Pushbutton [package="[SMD]"]
  Volume_- = Pushbutton [package="[SMD]"]
  C3 = Capacitor [package=0805]
  C4 = Capacitor [package=0805]
  Bone_Conduction_Transducer_Left = Vibration Motor- ROB-08449 [package=vibe-motor-10mm]
  Bone_Conduction_Transducer_Right = Vibration Motor- ROB-08449 [package=vibe-motor-10mm]
  C5 = Capacitor [package=0805]
  C6 = Capacitor [package=0805]
  C7 = Capacitor [package=0805]
  C8 = Capacitor [package=0805]

nets:
  N1: IC1.pin1, SMD_Cap_C1.1
  N2: IC1.pin2, C2.1
  N3: IC1.pin4, Volume_+.Pin_1, Volume_+.Pin_2
  N4: IC1.pin5, Volume_-.Pin_1, Volume_-.Pin_2
  N5: IC1.pin7, C3.1
  N6: IC1.pin8, C4.1
  N7: IC1.pin9, IC1.pin16, C7.2, C8.2
  N8: IC1.pin10, C6.2
  N9: IC1.pin11, Bone_Conduction_Transducer_Left.+
  N10: IC1.pin12, IC1.pin13
  N11: IC1.pin14, Bone_Conduction_Transducer_Right.+
  N12: IC1.pin15, C5.2
  N13: Volume_+.Pin_4, Volume_-.Pin_4
  N14: Bone_Conduction_Transducer_Left.-, C6.1
  N15: Bone_Conduction_Transducer_Right.-, C5.1
